# Fritzing sketch buzzer (saved by Fritzing 0.9.3b)
breadboards: 1

parts:
  Part1 = KY-006 Passive Buzzer Module [package="Breakout board"]
  U1 = NodeMCU V1.0

nets:
  N1: Part1.S, U1.3V3
  N2: Part1.-, U1.GND

custom parts:
  KY-006 Passive Buzzer Module: Passive Piezoelectric Buzzer Module Keyes KY-006, it can produce a range of sound tones depending on the input frequency.
  NodeMCU V1.0: ESP8266 based NodeMCU
