# Fritzing sketch switch-magnetic-door (saved by Fritzing 0.9.3b)
breadboards: 1

parts:
  S3 = Magnetic Door Switch [package=reed_switch_plastic]
  U1 = NodeMCU V1.0

nets:
  N1: S3.1, U1.GND
  N2: S3.2, U1.D2

custom parts:
  NodeMCU V1.0: ESP8266 based NodeMCU
