# Fritzing sketch flame-sensor (saved by Fritzing 0.9.3b)
breadboards: 1

parts:
  Part1 = KY-026 Flame Sensor Module [package="Breakout board"]
  U1 = NodeMCU V1.0

nets:
  N1: Part1.A0, U1.D4
  N2: Part1.G, U1.GND
  N3: Part1.+, U1.3V3
  N4: Part1.D0, U1.D3

custom parts:
  KY-026 Flame Sensor Module: KEYES KY-026 Arduino Flame Sensor Module reacts iin the presence of fire.
  NodeMCU V1.0: ESP8266 based NodeMCU
