# Fritzing sketch mq-6 (saved by Fritzing 0.9.3b)
breadboards: 1

parts:
  U1 = NodeMCU V1.0
  Part1 = MQ-7 breakout

nets:
  N1: U1.D2, Part1.AO
  N2: U1.D3, Part1.DO
  3V3: U1.3V3, Part1.VCC
  GND: U1.GND, Part1.GND

custom parts:
  NodeMCU V1.0: ESP8266 based NodeMCU
  MQ-7 breakout: SKU: 101282
