# Fritzing sketch PIR-HC-SR501 (saved by Fritzing 0.9.3b)
breadboards: 1

parts:
  PIR_HC-SR501 = HC-SR501 Body Sensor Module
  U1 = NodeMCU V1.0

nets:
  VCC: PIR_HC-SR501.VCC, U1.3V3
  N1: PIR_HC-SR501.OUT, U1.D7
  GND: PIR_HC-SR501.GND, U1.GND

custom parts:
  HC-SR501 Body Sensor Module: Pyroelectric Infrared PIR Motion Sensor Detector Module
  NodeMCU V1.0: ESP8266 based NodeMCU
