# Fritzing sketch raindrop-sensor (saved by Fritzing 0.9.3b)
breadboards: 1

parts:
  YL-83_-_Detection_Board1 = YL-83 Rain Sensor - Detection Board
  YL-83_-_Control_Board1 = YL-83 Rain Sensor - Control Board
  U1 = NodeMCU V1.0

nets:
  N1: YL-83_-_Detection_Board1.POS, YL-83_-_Control_Board1.POS
  N2: YL-83_-_Detection_Board1.NEG, YL-83_-_Control_Board1.NEG
  N3: YL-83_-_Control_Board1.DO, U1.D2

custom parts:
  YL-83 Rain Sensor - Detection Board: The YL-83 is a rain sensor that has more resistance when dry and less resistance when wet. The module runs at 5V.
  YL-83 Rain Sensor - Control Board: The YL-83 is a rain sensor that has more resistance when dry and less resistance when wet. The module runs at 5V.
  NodeMCU V1.0: ESP8266 based NodeMCU
